// Logisim project cpu.circ as structural Verilog: 1 circuit, main circuit cpu
module cpu (
  input  clk,
  input  [31:0] INSTRUCTION,
  input  [31:0] READ_DATA,
  output [31:0] WRITE_ADDRESS,
  output [31:0] PROGRAM_COUNTER,
  output [31:0] ra,
  output [31:0] sp,
  output [31:0] t0,
  output [31:0] t1,
  output [31:0] t2,
  output [31:0] s0,
  output [31:0] s1,
  output [31:0] a0,
  output [31:0] tohost,
  output [3:0] WRITE_ENABLE,
  output [31:0] WRITE_DATA
);

  wire ASel, BSel;
  wire [2:0] ImmSel;
  wire [31:0] A, adder_1_out, B, ID_INSTRUCTION, Read_Data_2, Result;

  Adder #(.width(32)) adder_1 (.a(PROGRAM_COUNTER), .b(32'h4), .out(adder_1_out));  // open: cin, cout
  Register #(.width(32)) PC (.D(adder_1_out), .clk(clk), .Q(PROGRAM_COUNTER));  // open: en, clr
  alu alu_1 (.Result(Result), .A(A), .B(B), .ALUSel(4'b0000));
  imm_gen imm_gen_1 (.inst(ID_INSTRUCTION), .ImmSel(ImmSel));  // open: imm
  control_logic control_logic_1 (
    .ASel(ASel), .BSel(BSel), .inst(ID_INSTRUCTION));  // open: CSRWen, PCSel, RegWEn, ImmSel, BrUn, ALUSel, MemRW, WBSel, CSRSel, BrEq, BrLt
  Register #(.width(32)) register_1 (.D(INSTRUCTION), .clk(clk), .Q(ID_INSTRUCTION));  // open: en, clr
  regfile regfile_1 (
    .rs1(ID_INSTRUCTION[19:15]), .rs2(ID_INSTRUCTION[24:20]), .rd(ID_INSTRUCTION[11:7]), .Write_Data(Result),
    .RegWEn(1'b1), .clk(clk), .ra(ra), .sp(sp), .t0(t0), .t1(t1), .t2(t2), .s0(s0), .s1(s1), .a0(a0),
    .Read_Data_1(A), .Read_Data_2(Read_Data_2));
  assign B = {{20{ID_INSTRUCTION[31]}}, ID_INSTRUCTION[31:20]};  // Bit_Extender bit_extender_1
  // csr csr_1: pin names not known; wires that end beside it: tohost
  Multiplexer #(.enable("false"), .width(32)) multiplexer_1 (.in0(A), .in1(PROGRAM_COUNTER));  // open: out, sel
  Multiplexer #(.enable("false"), .width(32)) multiplexer_2 (.in0(Read_Data_2), .in1(B));  // open: out, sel
  // branch_comp branch_comp_1: pin names not known

  // Other names for the same wires on the sheet: rd[4:0] = ID_INSTRUCTION[11:7]; rs1[4:0] = ID_INSTRUCTION[19:15];
  //   rs2[4:0] = ID_INSTRUCTION[24:20]; imm[31:0] = B; Read_Data_1[31:0] = A; Write_Data_t[31:0] = Result

  // Notes on the sheet:
  //   Output to IMEM
  //   TODO
  //   IMEM (do **NOT** move this)
  //   Inputs from IMEM
  //   IF
  //   ID
  //   EX
  //   JUST FOR ADDI !
  //   Inputs/Outputs for testing. Do **NOT** move these.
  //   TODO
  //   Outputs To DMEM
  //   DMEM (do **NOT** move this)
  //   Inputs From DMEM
endmodule
